// Logisim project p1.circ as structural Verilog: 1 circuit, main circuit main
module main (
  input  [31:0] in_1,
  input  [11:0] ADDRESS_BUS,
  input  in_3,
  input  in_4,
  input  in_5,
  input  [7:0] _0___read,
  input  [11:0] ADDRESS_BUS_2,
  input  in_8,
  input  in_9,
  input  in_10,
  output [31:0] _0___write,
  output [7:0] Data_Output
);

  wire not_1_out, not_2_out;
  wire [7:0] controlled_buffer_2_out;
  wire [31:0] controlled_buffer_1_out;

  not not_1 (not_1_out, in_9);
  not not_2 (not_2_out, in_4);
  assign controlled_buffer_1_out = in_4 ? in_1 : 32'bz;  // Controlled_Buffer controlled_buffer_1
  RAM #(.addrWidth(12), .dataWidth(32), .bus("asynch")) ram_1 (
    .addr(ADDRESS_BUS), .data(controlled_buffer_1_out), .sel(in_3), .ld(not_2_out), .clr(in_5));
  assign controlled_buffer_2_out = in_9 ? _0___read : 8'bz;  // Controlled_Buffer controlled_buffer_2
  RAM #(.addrWidth(12), .bus("asynch")) ram_2 (
    .addr(ADDRESS_BUS_2), .data(controlled_buffer_2_out), .sel(in_8), .ld(not_1_out), .clr(in_10));
  RAM #(.addrWidth(12), .bus("asynch")) ram_3 (
    .addr(ADDRESS_BUS_2), .data(controlled_buffer_2_out), .sel(in_8), .ld(not_1_out), .clr(in_10));
  RAM #(.addrWidth(12), .bus("asynch")) ram_4 (
    .addr(ADDRESS_BUS_2), .data(controlled_buffer_2_out), .sel(in_8), .ld(not_1_out), .clr(in_10));
  RAM #(.addrWidth(12), .bus("asynch")) ram_5 (
    .addr(ADDRESS_BUS_2), .data(controlled_buffer_2_out), .sel(in_8), .ld(not_1_out), .clr(in_10));
  assign _0___write = not_2_out ? controlled_buffer_1_out : 32'bz;  // Controlled_Buffer controlled_buffer_3
  assign Data_Output = not_1_out ? controlled_buffer_2_out : 8'bz;  // Controlled_Buffer controlled_buffer_4

  // Notes on the sheet:
  //   Address Input
  //   Address Input
  //   Data Input
  //   CONTROL BUS
  //   4096 x 32 bits
  //   DATA BUS
  //   CONTROL BUS
  //   4096 x 8 bits
  //   Data Input
  //   1/ write
  //   0 / read
  //   1/ write
  //   1/ read
  //   DATA BUS
  //   1/ read
  //   0 / write
  //   Data Output
endmodule
