// Logisim project 2ramSimulation.circ as structural Verilog: 1 circuit, main circuit main
module main (
  input  [3:0] LSB,
  input  [1:0] in_2,
  input  SEL,
  input  LEC,
  input  SAL,
  output MSB,
  output out_7,
  output out_8,
  output LSB_2
);

  wire not_1_out, not_2_out, not_3_out, not_4_out, undriven, undriven_2, undriven_3, undriven_4, undriven_5;

  not not_1 (not_1_out, in_2[0]);
  not not_2 (not_2_out, in_2[1]);
  not not_3 (not_3_out, in_2[1]);
  not not_4 (not_4_out, in_2[0]);
  // AND_Gate and_1 has open pins: in0=not_1_out, in1=not_2_out, out=open
  // AND_Gate and_2 has open pins: in0=not_3_out, in1=in_2[0], out=open
  // AND_Gate and_3 has open pins: in0=in_2[1], in1=not_4_out, out=open
  // AND_Gate and_4 has open pins: in0=in_2[0], in1=in_2[1], out=open
  // AND_Gate and_5 is placed but not wired
  // AND_Gate and_6 is placed but not wired
  // AND_Gate and_7 is placed but not wired
  // AND_Gate and_8 is placed but not wired
  // AND_Gate and_9 is placed but not wired
  // NOT_Gate not_5 is placed but not wired
  // AND_Gate and_10 is placed but not wired
  D_Flip_Flop d_ff_1 (.clk(undriven));  // open: D, Q, Qn, preset, en, reset
  // AND_Gate and_11 is placed but not wired
  D_Flip_Flop d_ff_2 ();  // open: clk, D, Q, Qn, preset, en, reset
  // AND_Gate and_12 is placed but not wired
  D_Flip_Flop d_ff_3 ();  // open: clk, D, Q, Qn, preset, en, reset
  // AND_Gate and_13 is placed but not wired
  D_Flip_Flop d_ff_4 ();  // open: clk, D, Q, Qn, preset, en, reset
  // AND_Gate and_14 is placed but not wired
  // OR_Gate or_1 is placed but not wired
  buf and_15 (LSB_2, undriven_3);  // AND_Gate
  D_Flip_Flop d_ff_5 (.clk(undriven_2));  // open: D, Q, Qn, preset, en, reset
  D_Flip_Flop d_ff_6 ();  // open: clk, D, Q, Qn, preset, en, reset
  D_Flip_Flop d_ff_7 ();  // open: clk, D, Q, Qn, preset, en, reset
  D_Flip_Flop d_ff_8 ();  // open: clk, D, Q, Qn, preset, en, reset
  buf and_16 (out_8, undriven_3);  // AND_Gate
  // AND_Gate and_17 is placed but not wired
  // AND_Gate and_18 is placed but not wired
  // AND_Gate and_19 is placed but not wired
  // AND_Gate and_20 is placed but not wired
  // OR_Gate or_2 is placed but not wired
  buf and_21 (out_7, undriven_3);  // AND_Gate
  D_Flip_Flop d_ff_9 (.clk(undriven_4));  // open: D, Q, Qn, preset, en, reset
  // AND_Gate and_22 is placed but not wired
  D_Flip_Flop d_ff_10 ();  // open: clk, D, Q, Qn, preset, en, reset
  // AND_Gate and_23 is placed but not wired
  D_Flip_Flop d_ff_11 ();  // open: clk, D, Q, Qn, preset, en, reset
  // AND_Gate and_24 is placed but not wired
  D_Flip_Flop d_ff_12 ();  // open: clk, D, Q, Qn, preset, en, reset
  // AND_Gate and_25 is placed but not wired
  // OR_Gate or_3 is placed but not wired
  buf and_26 (MSB, undriven_3);  // AND_Gate
  D_Flip_Flop d_ff_13 (.clk(undriven_5));  // open: D, Q, Qn, preset, en, reset
  // AND_Gate and_27 is placed but not wired
  D_Flip_Flop d_ff_14 ();  // open: clk, D, Q, Qn, preset, en, reset
  // AND_Gate and_28 is placed but not wired
  D_Flip_Flop d_ff_15 ();  // open: clk, D, Q, Qn, preset, en, reset
  // AND_Gate and_29 is placed but not wired
  D_Flip_Flop d_ff_16 ();  // open: clk, D, Q, Qn, preset, en, reset
  // AND_Gate and_30 is placed but not wired
  // OR_Gate or_4 is placed but not wired

  // Notes on the sheet:
  //   ADDRESSES
  //   chip select
  //   read/write
  //   Output enable
  //   MSB
  //   MSB
  //   1
  //   2
  //   4
  //   3
endmodule
