// Logisim project p2RegMem.circ as structural Verilog: 1 circuit, main circuit main
module main (
  input  [9:0] in_1,
  input  Clear,
  input  [3:0] Data_Input,
  input  in_4,
  output [3:0] out_5
);

  wire and_1_out, and_2_out, and_3_out, and_4_out, nand_1_out, nand_2_out, nand_3_out, not_1_out, not_2_out,
       not_3_out, not_4_out, not_5_out, not_6_out, not_7_out;
  wire [3:0] controlled_buffer_1_out, controlled_buffer_2_out, controlled_buffer_3_out,
       controlled_buffer_4_out, controlled_buffer_5_out, register_1_q, register_2_q, register_3_q,
       register_4_q;

  nand nand_1 (nand_1_out, ~in_1[4], ~in_1[5], ~in_1[6], ~in_1[7], in_1[8], in_1[9]);  // NAND_Gate
  not not_1 (not_1_out, in_1[3]);
  not not_2 (not_2_out, nand_2_out);
  nand nand_2 (nand_2_out, in_1[3], ~nand_1_out);  // NAND_Gate
  not not_3 (not_3_out, nand_3_out);
  nand nand_3 (nand_3_out, ~nand_1_out, not_1_out);  // NAND_Gate
  assign controlled_buffer_1_out = not_2_out ? Data_Input : 4'bz;  // Controlled_Buffer controlled_buffer_1
  not not_4 (not_4_out, in_1[0]);
  not not_5 (not_5_out, in_1[1]);
  not not_6 (not_6_out, in_1[1]);
  not not_7 (not_7_out, in_1[0]);
  and and_1 (and_1_out, not_4_out, not_5_out);
  and and_2 (and_2_out, in_1[0], not_6_out);
  and and_3 (and_3_out, not_7_out, in_1[1]);
  and and_4 (and_4_out, in_1[0], in_1[1]);
  assign controlled_buffer_2_out = not_3_out ? register_1_q : 4'bz;  // Controlled_Buffer controlled_buffer_2
  Register #(.width(4), .trigger("high")) register_1 (
    .D(controlled_buffer_1_out), .en(and_1_out), .Q(register_1_q), .clk(in_4), .clr(Clear));
  Register #(.width(4), .trigger("high")) register_2 (
    .D(controlled_buffer_1_out), .en(and_2_out), .Q(register_2_q), .clk(in_4), .clr(Clear));
  Register #(.width(4), .trigger("high")) register_3 (
    .D(controlled_buffer_1_out), .en(and_3_out), .Q(register_3_q), .clk(in_4), .clr(Clear));
  Register #(.width(4), .trigger("high")) register_4 (
    .D(controlled_buffer_1_out), .en(and_4_out), .Q(register_4_q), .clk(in_4), .clr(Clear));
  assign controlled_buffer_3_out = not_3_out ? register_2_q : 4'bz;  // Controlled_Buffer controlled_buffer_3
  assign controlled_buffer_4_out = not_3_out ? register_3_q : 4'bz;  // Controlled_Buffer controlled_buffer_4
  Multiplexer #(.select(2), .width(4)) multiplexer_1 (
    .in0(controlled_buffer_2_out), .in1(controlled_buffer_3_out), .in2(controlled_buffer_4_out),
    .in3(controlled_buffer_5_out), .out(out_5), .sel(in_1[1:0]), .en(not_3_out));
  assign controlled_buffer_5_out = not_3_out ? register_4_q : 4'bz;  // Controlled_Buffer controlled_buffer_5

  // Notes on the sheet:
  //   L =  0 escritura puerto salida
  //   L = 1 lectura puerto entrada
  //   read
  //   write
endmodule
