// Logisim project p2a.circ as structural Verilog: 1 circuit, main circuit main
module main (
  input  [31:0] Bus_de_Datos,
  input  Bus_de_Control,
  input  in_3,
  input  [15:0] in_4,
  input  [31:0] in_5,
  input  Bus_de_Control_2,
  input  [15:0] in_7,
  output [31:0] out_8,
  output [31:0] Bus_de_Datos_2
);

  wire and_1_out, and_2_out, and_3_out, nand_1_out, not_1_out, not_2_out, not_3_out, not_4_out, not_5_out,
       not_6_out, not_7_out, not_8_out, not_9_out, not_10_out, not_11_out;
  wire [31:0] controlled_buffer_1_out, register_1_q;

  not not_1 (not_1_out, in_4[0]);
  not not_2 (not_2_out, in_4[3]);
  not not_3 (not_3_out, in_4[5]);
  not not_4 (not_4_out, in_4[7]);
  not not_5 (not_5_out, in_4[9]);
  not not_6 (not_6_out, in_4[10]);
  not not_7 (not_7_out, in_4[13]);
  not not_8 (not_8_out, in_4[14]);
  not not_9 (not_9_out, in_4[15]);
  nand nand_1 (nand_1_out, ~not_1_out, ~in_4[1], ~in_4[2], ~not_2_out, ~in_4[4], ~not_3_out, ~in_4[6], ~not_4_out, ~in_4[8], ~not_5_out, ~not_6_out, ~in_4[11], ~in_4[12], ~not_7_out, ~not_8_out, ~not_9_out);  // NAND_Gate
  and and_1 (and_1_out, ~in_7[0], ~in_7[1], ~in_7[2], in_7[3], ~in_7[4], in_7[5], ~in_7[6], in_7[7], ~in_7[8], in_7[9], in_7[10], ~in_7[11], ~in_7[12], in_7[13], in_7[14], in_7[15]);  // AND_Gate
  assign controlled_buffer_1_out = and_2_out ? Bus_de_Datos : 32'bz;  // Controlled_Buffer controlled_buffer_1
  and and_2 (and_2_out, ~nand_1_out, Bus_de_Control);  // AND_Gate
  and and_3 (and_3_out, and_1_out, Bus_de_Control_2);
  Register #(.width(32), .trigger("falling")) register_1 (
    .D(controlled_buffer_1_out), .Q(register_1_q), .clk(and_2_out), .clr(in_3));  // open: en
  not not_10 (not_10_out, and_2_out);
  assign Bus_de_Datos_2 = not_11_out ? in_5 : 32'bz;  // Controlled_Buffer controlled_buffer_2
  not not_11 (not_11_out, and_3_out);
  assign out_8 = not_10_out ? register_1_q : 32'bz;  // Controlled_Buffer controlled_buffer_3

  // Notes on the sheet:
  //   Puerto de Salida
  //   D6A9H
  //   Puerto de Entrada
  //   D6A8H
  //   Bus de Direcciones
  //   Bus de Direcciones
  //   IOWR
  //   IOWR
  //   Bus de Datos
endmodule
