// Logisim project p3a.circ as structural Verilog: 2 circuits, main circuit main
module main (
  input  [7:0] in_1,
  input  [7:0] in_2,
  input  CARRY,
  input  [3:0] Select_Operation,
  input  Enable,
  output Overflow,
  output Zero,
  output [7:0] Result,
  output Carry_Out
);

  wire adder_1_cout, adder_2_cout, subtractor_1_bout, subtractor_2_bout;
  wire [7:0] adder_1_out, adder_2_out, adder_3_out, and_1_out, not_1_out, or_1_out, shifter_1_out,
       shifter_2_out, shifter_3_out, shifter_4_out, subtractor_1_out, subtractor_2_out, subtractor_3_out,
       xor_1_out;

  assign and_1_out = in_1 & in_2;  // AND_Gate and_1, 8 bits wide
  assign or_1_out = in_1 | in_2;  // OR_Gate or_1, 8 bits wide
  assign xor_1_out = in_1 ^ in_2;  // XOR_Gate xor_1, 8 bits wide
  assign not_1_out = ~in_1;  // NOT_Gate not_1, 8 bits wide
  Adder adder_1 (.a(in_1), .b(in_2), .out(adder_1_out), .cout(adder_1_cout));  // open: cin
  Adder adder_2 (.a(in_1), .b(in_2), .out(adder_2_out), .cin(CARRY), .cout(adder_2_cout));
  Subtractor subtractor_1 (.a(in_2), .b(in_1), .out(subtractor_1_out), .bout(subtractor_1_bout));  // open: bin
  Subtractor subtractor_2 (.a(in_2), .b(in_1), .out(subtractor_2_out), .bin(CARRY), .bout(subtractor_2_bout));
  Adder adder_3 (.a(in_1), .b(8'h1), .out(adder_3_out));  // open: cin, cout
  Subtractor subtractor_3 (.a(8'h1), .b(in_1), .out(subtractor_3_out));  // open: bin, bout
  Shifter shifter_1 (.in(in_1), .\dist (3'b001), .out(shifter_1_out));
  Shifter #(.shift("lr")) shifter_2 (.in(in_1), .\dist (3'b001), .out(shifter_2_out));
  Shifter #(.shift("rl")) shifter_3 (.in(in_1), .\dist (3'b001), .out(shifter_3_out));
  Shifter #(.shift("rr")) shifter_4 (.in(in_1), .\dist (3'b001), .out(shifter_4_out));
  Multiplexer #(.select(4), .width(8)) multiplexer_1 (
    .in0(and_1_out), .in1(or_1_out), .in2(xor_1_out), .in3(not_1_out), .in4(adder_1_out), .in5(adder_2_out),
    .in6(subtractor_1_out), .in7(subtractor_2_out), .in8(adder_3_out), .in9(subtractor_3_out),
    .in10(shifter_1_out), .in11(shifter_2_out), .in12(shifter_3_out), .in13(shifter_4_out), .out(Result),
    .sel(Select_Operation), .en(Enable));  // open: in14, in15
  Cout cout_1 (
    .ADD(adder_1_cout), .ADC(adder_2_cout), .SUB(subtractor_1_bout), .SBB(subtractor_2_bout),
    .out_6(Carry_Out), .in_1(Select_Operation));
  Comparator comparator_1 (.a(Result), .b({8{1'b1}}), .gt(Overflow));  // open: eq, lt
  Comparator comparator_2 (.a(Result), .b({8{1'b0}}), .eq(Zero));  // open: gt, lt

  // Notes on the sheet:
  //   A
  //   B
  //   Operations
  //   0000 AND  A,B
  //   0001 OR  A,B
  //   0010 XOR A,B
  //   0011 NOT   A
  //   0100 ADD  A,B
  //   0101 ADC  A,B
  //   0110 SUB  B,A
  //   0111 SBB  B,A
  //   1000 INC  A
  //   1001 DEC  A
  //   1010  SHL  A
  //   1011  SHR  A
  //   1100 ROL  A
  //   1101 ROR  A
endmodule

module Cout (
  input  [3:0] in_1,
  input  ADD,
  input  ADC,
  input  SUB,
  input  SBB,
  output out_6
);

  wire and_1_out, and_2_out, and_3_out, and_4_out;

  and and_1 (and_1_out, ADD, ~in_1[3], in_1[2], ~in_1[1], ~in_1[0]);  // AND_Gate
  and and_2 (and_2_out, ADC, ~in_1[3], in_1[2], ~in_1[1], in_1[0]);  // AND_Gate
  and and_3 (and_3_out, SUB, ~in_1[3], in_1[2], in_1[1], ~in_1[0]);  // AND_Gate
  and and_4 (and_4_out, SBB, ~in_1[3], in_1[2], in_1[1], in_1[0]);  // AND_Gate
  or or_1 (out_6, and_1_out, and_2_out, and_3_out, and_4_out);

  // Notes on the sheet:
  //   0100
  //   0110
  //   0111
  //   0101
  //   Arithmetic operation code
endmodule
