// Logisim project p3b - copia.circ as structural Verilog: 1 circuit, main circuit main
module main (
  input  [3:0] RS,
  input  [3:0] RD,
  input  in_3,
  input  [5:0] OP_CC_TT,
  output Overflow_flag,
  output out_6,
  output [3:0] Result,
  output out_8
);

  wire adder_1_cout, adder_2_cout, controlled_inverter_1_out, decoder_1_out0, decoder_1_out1, decoder_1_out2,
       decoder_1_out3, multiplexer_2_out, subtractor_1_bout;
  wire [3:0] adder_1_out, adder_2_out, and_1_out, or_1_out, subtractor_1_out, xor_1_out;

  Decoder #(.select(2), .enable("false")) decoder_1 (
    .out0(decoder_1_out0), .out1(decoder_1_out1), .out2(decoder_1_out2), .out3(decoder_1_out3),
    .sel(OP_CC_TT[3:2]));
  assign controlled_inverter_1_out = decoder_1_out0 ? ~decoder_1_out0 : 1'bz;  // Controlled_Inverter controlled_inverter_1
  assign controlled_inverter_1_out = decoder_1_out1 ? decoder_1_out1 : 1'bz;  // Controlled_Buffer controlled_buffer_1
  assign controlled_inverter_1_out = decoder_1_out2 ? out_8 : 1'bz;  // Controlled_Buffer controlled_buffer_2
  assign controlled_inverter_1_out = decoder_1_out3 ? ~out_8 : 1'bz;  // Controlled_Inverter controlled_inverter_2
  Adder #(.width(4)) adder_1 (.a(RD), .b(RS), .out(adder_1_out), .cin(controlled_inverter_1_out), .cout(adder_1_cout));
  Adder #(.width(4)) adder_2 (.a(RD), .b(RS), .out(adder_2_out), .cin(controlled_inverter_1_out), .cout(adder_2_cout));
  Subtractor #(.width(4)) subtractor_1 (
    .a(RD), .b(RS), .out(subtractor_1_out), .bin(controlled_inverter_1_out), .bout(subtractor_1_bout));
  assign and_1_out = RD & RS;  // AND_Gate and_1, 4 bits wide
  assign or_1_out = RD | RS;  // OR_Gate or_1, 4 bits wide
  assign xor_1_out = RD ^ RS;  // XOR_Gate xor_1, 4 bits wide
  Multiplexer #(.select(4), .width(4), .enable("false")) multiplexer_1 (
    .in0(adder_1_out), .in4(adder_2_out), .in8(subtractor_1_out), .in13(or_1_out), .in14(and_1_out),
    .in15(xor_1_out), .out(Result), .sel({OP_CC_TT[5:4], OP_CC_TT[1:0]}));  // open: in1, in2, in3, in5, in6, in7, in9, in10, in11, in12
  Comparator #(.width(4)) comparator_1 (.a(Result), .b(4'b1111), .gt(Overflow_flag));  // open: eq, lt
  Comparator #(.width(4), .mode("unsigned")) comparator_2 (.a(Result), .b(4'b0000), .eq(out_6));  // open: gt, lt
  Register #(.width(1), .trigger("high")) register_1 (.D(multiplexer_2_out), .Q(out_8), .clk(in_3));  // open: en, clr
  Multiplexer #(.select(4), .enable("false")) multiplexer_2 (
    .in0(adder_1_cout), .in4(adder_2_cout), .in8(subtractor_1_bout), .out(multiplexer_2_out),
    .sel({OP_CC_TT[5:4], OP_CC_TT[1:0]}));  // open: in1, in2, in3, in5, in6, in7, in9, in10, in11, in12, in13, in14, in15

  // Notes on the sheet:
  //   Zero flag
  //   Cout
endmodule
